# Fritzing sketch fritzing_1 (saved by Fritzing 0.9.3b)
breadboards: 1

parts:
  U1 = NodeMCU V1.0
  부품1 = Humidity Sensor - HIH-4030 Breakout

nets:
  N1: U1.D3, U1.D4, 부품1.OUT
  3V3: U1.3V3, 부품1.VCC
  GND: U1.GND, 부품1.GND

custom parts:
  NodeMCU V1.0: ESP8266 based NodeMCU
