# Fritzing sketch fritzing_3 (saved by Fritzing 0.9.3b)
breadboards: 1

parts:
  U1 = NodeMCU V1.0
  부품1 = Humidity Sensor - HIH-4030 Breakout
  부품2 = LCD1602-I2C

nets:
  N1: U1.D1, 부품2.SCL
  N2: U1.D2, 부품2.SDA
  N3: U1.D3, U1.D4, 부품1.OUT
  VCC: U1.3V3, 부품1.VCC, 부품2.VCC
  GND: U1.GND, 부품1.GND, 부품2.GND

custom parts:
  NodeMCU V1.0: ESP8266 based NodeMCU
  LCD1602-I2C: A standard character display, usually with 2x16 characters. Comes in many colors with LCM1602 IIC attached.
